// Digital circuit Project_Potato.dig as structural Verilog
module Project_Potato (
  input  clk,
  input  in_2,
  input  in_3,
  input  in_4,
  input  in_5,
  input  in_6,
  input  in_7,
  input  in_8,
  input  in_9
);

  wire _7448_1_p10, _7448_1_p11, _7448_1_p12, _7448_1_p13, _7448_1_p14, _7448_1_p15, _7448_1_p16,
       decoder_1_out_1, decoder_1_out_4, Halt_Command, multiplexer_1_out, R_out, undriven, undriven_2,
       undriven_3, undriven_4;
  wire [3:0] add_1_s, counter_1_out, RegA_q, RegB_q;
  wire [7:0] rom_1_d;

  Multiplexer multiplexer_1 (.sel(Halt_Command), .in_0(in_2), .in_1(in_3), .out(multiplexer_1_out));
  Button R (.out(R_out));
  LED led_1 (.in(undriven));
  LED led_2 (.in(undriven_2));
  LED led_3 (.in(undriven_3));
  Counter #(.Bits(4)) counter_1 (.en(multiplexer_1_out), .C(clk), .clr(R_out), .out(counter_1_out));  // open: ovf
  LED led_4 (.in(undriven_4));
  ROM #(.AddrBits(4), .Bits(8)) rom_1 (.A(counter_1_out), .sel(in_5), .D(rom_1_d));
  LED led_5 (.in(rom_1_d[7]));
  LED led_6 (.in(rom_1_d[6]));
  LED led_7 (.in(rom_1_d[5]));
  LED led_8 (.in(rom_1_d[4]));
  LED led_9 (.in(rom_1_d[3]));
  LED led_10 (.in(rom_1_d[2]));
  LED led_11 (.in(rom_1_d[1]));
  LED led_12 (.in(rom_1_d[0]));
  Decoder #(.Selector_Bits(4)) decoder_1 (
    .sel(rom_1_d[7:4]), .out_1(decoder_1_out_1), .out_4(decoder_1_out_4), .out_15(Halt_Command));  // open: out_0, out_2, out_3, out_5, out_6, out_7, out_8, out_9, out_10, out_11, out_12, out_13, out_14
  Register #(.Bits(4)) RegA (.D(rom_1_d[3:0]), .C(decoder_1_out_1), .en(in_4), .Q(RegA_q));
  Register #(.Bits(4)) RegB (.D(rom_1_d[3:0]), .C(decoder_1_out_4), .en(in_8), .Q(RegB_q));
  Add #(.Bits(4)) add_1 (.a(RegB_q), .b(RegA_q), .c_i(in_9), .s(add_1_s));  // open: c_o
  // _7448 _7448_1: pin names not known; wires that end beside it: in_6, in_7, add_1_s[0], add_1_s[1], add_1_s[2], add_1_s[3], in_6, in_6, in_6, _7448_1_p10, _7448_1_p11, _7448_1_p12, _7448_1_p13, _7448_1_p14, _7448_1_p15, _7448_1_p16
  Seven_Seg seven_seg_1 (
    .a(_7448_1_p10), .b(_7448_1_p11), .c(_7448_1_p12), .d(_7448_1_p13), .e(_7448_1_p14), .f(_7448_1_p15),
    .g(_7448_1_p16), .dp(in_7));

  // Notes on the sheet:
  //   in_2: default 1
  //   in_4: default 1
  //   in_5: default 1
  //   in_6: default 1
  //   in_8: default 1
  //   contents of rom_1 (hex, n*v repeats v):
  //   14,44,f0
endmodule
